// Logisim project oblig01syhd.circ as structural Verilog: 3 circuits, main circuit Multiplicator
module Multiplicator (
  input  A,
  input  B,
  input  C,
  input  D,
  input  Switch,
  output R8,
  output R7,
  output R6,
  output R5,
  output R4,
  output R3,
  output R2,
  output R1,
  output R0
);

  wire full_adder_1_cout, full_adder_1_sum, half_adder_2_cout, half_adder_3_cout, half_adder_3_sum,
       half_adder_4_cout, half_adder_5_cout, half_adder_5_sum, half_adder_6_cout, half_adder_7_cout,
       half_adder_8_cout, half_adder_8_sum, half_adder_9_cout, half_adder_10_cout, half_adder_11_cout,
       half_adder_12_cout, xor_1_out, xor_2_out, xor_3_out, xor_4_out, xor_5_out, xor_6_out, xor_7_out;

  Half_Adder half_adder_1 (.x(Switch), .y(half_adder_2_cout), .Sum(R8));  // open: Cout
  xor xor_1 (xor_1_out, half_adder_3_cout, Switch);
  Half_Adder half_adder_2 (.x(xor_1_out), .y(half_adder_4_cout), .Sum(R7), .Cout(half_adder_2_cout));
  Half_Adder half_adder_3 (.x(A), .y(half_adder_5_cout), .Sum(half_adder_3_sum), .Cout(half_adder_3_cout));
  xor xor_2 (xor_2_out, half_adder_3_sum, Switch);
  Half_Adder half_adder_4 (.x(xor_2_out), .y(half_adder_6_cout), .Sum(R6), .Cout(half_adder_4_cout));
  Half_Adder half_adder_5 (.x(B), .y(full_adder_1_cout), .Sum(half_adder_5_sum), .Cout(half_adder_5_cout));
  xor xor_3 (xor_3_out, half_adder_5_sum, Switch);
  Half_Adder half_adder_6 (.x(xor_3_out), .y(half_adder_7_cout), .Sum(R5), .Cout(half_adder_6_cout));
  Full_Adder full_adder_1 (.x(A), .y(C), .Sum(full_adder_1_sum), .Cout(full_adder_1_cout), .Cin(half_adder_8_cout));
  xor xor_4 (xor_4_out, full_adder_1_sum, Switch);
  Half_Adder half_adder_7 (.x(xor_4_out), .y(half_adder_9_cout), .Sum(R4), .Cout(half_adder_7_cout));
  Half_Adder half_adder_8 (.x(B), .y(D), .Sum(half_adder_8_sum), .Cout(half_adder_8_cout));
  xor xor_5 (xor_5_out, half_adder_8_sum, Switch);
  Half_Adder half_adder_9 (.x(xor_5_out), .y(half_adder_10_cout), .Sum(R3), .Cout(half_adder_9_cout));
  xor xor_6 (xor_6_out, C, Switch);
  Half_Adder half_adder_10 (.x(xor_6_out), .y(half_adder_11_cout), .Sum(R2), .Cout(half_adder_10_cout));
  xor xor_7 (xor_7_out, D, Switch);
  Half_Adder half_adder_11 (.x(xor_7_out), .y(half_adder_12_cout), .Sum(R1), .Cout(half_adder_11_cout));
  Half_Adder half_adder_12 (.x(Switch), .y(Switch), .Sum(R0), .Cout(half_adder_12_cout));

  // Notes on the sheet:
  //   Brukernavn: syhd
  //   INF2270 - Oblig 1
endmodule

// HA
module Half_Adder (
  input  x,
  input  y,
  output Sum,
  output Cout
);

  xor xor_1 (Sum, x, y);
  and and_1 (Cout, x, y);

  // Notes on the sheet:
  //   NB: Implementasjonen min for half-adder (HA) er samme som den som står i forelesningsfoilene
endmodule

// FA
module Full_Adder (
  input  x,
  input  y,
  input  Cin,
  output Sum,
  output Cout
);

  wire and_1_out, and_2_out, xor_1_out;

  xor xor_1 (xor_1_out, x, y);
  and and_1 (and_1_out, x, y);
  xor xor_2 (Sum, xor_1_out, Cin);
  and and_2 (and_2_out, xor_1_out, Cin);
  or or_1 (Cout, and_2_out, and_1_out);

  // Notes on the sheet:
  //   NB: Implementasjonen min for full-adder (FA) er samme som den som står i forelesningsfoilene
endmodule
