// Logisim project Oblig2syhd.circ as structural Verilog: 4 circuits, main circuit main
module main (
);

  wire Clock_out, control_unit_1_c1___8, control_unit_1_c2___9, control_unit_1_c3___8__or__b,
       control_unit_1_c4___9__or__b, control_unit_1_c5___a__or__b, control_unit_1_c6___a, Reset_out;
  wire [3:0] counter_1_output;
  wire [7:0] ram_1_data, ram_2_data, register_1_q;

  Counter counter_1 (.Output(counter_1_output), .Clk(Clock_out), .Reset(Reset_out));
  Clock Clock (.out(Clock_out));
  Button Reset (.out(Reset_out));
  RAM #(.addrWidth(4), .bus("asynch")) ram_1 (
    .addr(counter_1_output), .data(ram_1_data), .sel(1'b1), .ld(1'b1), .clr(1'b0));
  Control_Unit control_unit_1 (
    .C1___8(control_unit_1_c1___8), .C2___9(control_unit_1_c2___9),
    .C3___8__or__B(control_unit_1_c3___8__or__b), .C4___9__or__B(control_unit_1_c4___9__or__b),
    .C5___A__or__B(control_unit_1_c5___a__or__b), .C6___A(control_unit_1_c6___a),
    .operation_code_star_star(ram_1_data[7:4]));
  RAM #(.addrWidth(4)) ram_2 (
    .addr(ram_1_data[3:0]), .data(ram_2_data), .sel(control_unit_1_c5___a__or__b), .clk(Clock_out),
    .ld(control_unit_1_c6___a), .clr(Reset_out));
  assign ram_2_data[3:0] = control_unit_1_c1___8 ? ram_1_data[3:0] : 4'bz;  // Controlled_Buffer controlled_buffer_1
  assign ram_2_data[7:4] = control_unit_1_c2___9 ? ram_1_data[3:0] : 4'bz;  // Controlled_Buffer controlled_buffer_2
  Register register_1 (.D(ram_2_data), .Q(register_1_q), .clk(Clock_out), .clr(Reset_out));  // open: en
  assign ram_2_data[3:0] = control_unit_1_c4___9__or__b ? register_1_q[3:0] : 4'bz;  // Controlled_Buffer controlled_buffer_3
  assign ram_2_data[7:4] = control_unit_1_c3___8__or__b ? register_1_q[7:4] : 4'bz;  // Controlled_Buffer controlled_buffer_4

  // Notes on the sheet:
  //   Brukernavn: syhd
  //   INF2270 Oblig2 - Vår 2016
  //   Program Memory
  //   Data Memory
  //   System Bus
endmodule

// Control Logic
module Control_Unit (
  input  [3:0] operation_code_star_star,
  output C1___8,
  output C2___9,
  output C3___8__or__B,
  output C4___9__or__B,
  output C5___A__or__B,
  output C6___A
);

  wire decoder_1_out11;

  Decoder #(.select(4), .enable("false")) decoder_1 (
    .out8(C1___8), .out9(C2___9), .out10(C6___A), .out11(decoder_1_out11), .sel(operation_code_star_star));  // open: out0, out1, out2, out3, out4, out5, out6, out7, out12, out13, out14, out15
  or or_1 (C3___8__or__B, C1___8, decoder_1_out11);
  or or_2 (C4___9__or__B, C2___9, decoder_1_out11);
  or or_3 (C5___A__or__B, C6___A, decoder_1_out11);

  // Notes on the sheet:
  //   **Operation-code bør være enten 8(1000), 9(1001), A(1010), eller B(1011)
endmodule

// Count
module Counter (
  input  Clk,
  input  Reset,
  output [3:0] Output
);

  wire half_adder_1_carry, half_adder_1_sum, half_adder_2_carry, half_adder_2_sum, half_adder_3_carry,
       half_adder_3_sum, half_adder_4_carry, half_adder_4_sum;
  wire [3:0] or_4_out;

  Half_Adder half_adder_1 (.A(Output[3]), .B(half_adder_2_carry), .Sum(half_adder_1_sum), .Carry(half_adder_1_carry));
  or or_1 (or_4_out[3], half_adder_1_carry, half_adder_1_sum);
  Half_Adder half_adder_2 (.A(Output[2]), .B(half_adder_3_carry), .Sum(half_adder_2_sum), .Carry(half_adder_2_carry));
  or or_2 (or_4_out[2], half_adder_1_carry, half_adder_2_sum);
  Half_Adder half_adder_3 (.A(Output[1]), .B(half_adder_4_carry), .Sum(half_adder_3_sum), .Carry(half_adder_3_carry));
  or or_3 (or_4_out[1], half_adder_1_carry, half_adder_3_sum);
  Half_Adder half_adder_4 (.A(Output[0]), .B(1'b1), .Sum(half_adder_4_sum), .Carry(half_adder_4_carry));
  or or_4 (or_4_out[0], half_adder_1_carry, half_adder_4_sum);
  Register #(.width(4)) register_1 (.D(or_4_out), .Q(Output), .clk(Clk), .clr(Reset));  // open: en
endmodule

// HA
module Half_Adder (
  input  A,
  input  B,
  output Sum,
  output Carry
);

  xor xor_1 (Sum, A, B);
  and and_1 (Carry, A, B);
endmodule
